// Logisim project aula1.circ as structural Verilog
module ALUcinado (
  input  in_1
);

  Mux2x1 mux2x1_1 (.selectPin(in_1));  // open: in0, in1, out0
  Adder adder_1 ();  // open: a, b, out, cin, cout
endmodule
