// Logisim project forfun.circ as structural Verilog: 6 circuits, main circuit main
module main (
);

  PC pc_1 ();  // open: in_in, Enable, Reset, in_out
endmodule

module register_bank (
);

  wire [31:0] undriven;

  Register #(.width(32)) register_1 (.D(undriven));  // open: en, clk, Q, clr
  Register #(.width(32)) register_2 ();  // open: D, en, Q, clk, clr
  Register #(.width(32)) register_3 ();  // open: D, en, Q, clk, clr
  Register #(.width(32)) register_4 ();  // open: D, en, Q, clk, clr
  Register #(.width(32)) register_5 ();  // open: D, en, Q, clk, clr
  Register #(.width(32)) register_6 ();  // open: D, en, Q, clk, clr
  Register #(.width(32)) register_7 ();  // open: D, en, Q, clk, clr
  Register #(.width(32)) register_8 ();  // open: D, en, Q, clk, clr
  Register #(.width(32)) register_9 ();  // open: D, en, Q, clk, clr
  Register #(.width(32)) register_10 ();  // open: D, en, Q, clk, clr
  Register #(.width(32)) register_11 ();  // open: D, en, Q, clk, clr
  Register #(.width(32)) register_12 ();  // open: D, en, Q, clk, clr
  Register #(.width(32)) register_13 ();  // open: D, en, Q, clk, clr
  Register #(.width(32)) register_14 ();  // open: D, en, Q, clk, clr
  Register #(.width(32)) register_15 ();  // open: D, en, Q, clk, clr
  Register #(.width(32)) register_16 ();  // open: D, en, Q, clk, clr
  Register #(.width(32)) register_17 ();  // open: D, en, Q, clk, clr
  Register #(.width(32)) register_18 ();  // open: D, en, Q, clk, clr
  Register #(.width(32)) register_19 ();  // open: D, en, Q, clk, clr
  Register #(.width(32)) register_20 ();  // open: D, en, Q, clk, clr
  Register #(.width(32)) register_21 ();  // open: D, en, Q, clk, clr
  Register #(.width(32)) register_22 ();  // open: D, en, Q, clk, clr
  Register #(.width(32)) register_23 ();  // open: D, en, Q, clk, clr
  Register #(.width(32)) register_24 ();  // open: D, en, Q, clk, clr
  Register #(.width(32)) register_25 ();  // open: D, en, Q, clk, clr
  Register #(.width(32)) register_26 ();  // open: D, en, Q, clk, clr
  Register #(.width(32)) register_27 ();  // open: D, en, Q, clk, clr
  Register #(.width(32)) register_28 ();  // open: D, en, Q, clk, clr
  Register #(.width(32)) register_29 ();  // open: D, en, Q, clk, clr
  Register #(.width(32)) register_30 ();  // open: D, en, Q, clk, clr
  Register #(.width(32)) register_31 ();  // open: D, en, Q, clk, clr
  Register #(.width(32)) register_32 ();  // open: D, en, Q, clk, clr
endmodule

module fetch (
  input  Enable,
  input  Reset,
  output [31:0] instruction
);

  wire clk_out;
  wire [31:0] program_counter_q;

  Register #(.width(32)) program_counter (
    .D(instruction), .en(Enable), .clk(clk_out), .Q(program_counter_q), .clr(Reset));
  Clock clk (.out(clk_out));
  Adder #(.width(32)) adder_1 (.a(program_counter_q), .b(32'h4), .out(instruction));  // open: cin, cout
endmodule

module PC (
  input  [31:0] in_in,
  input  Enable,
  input  Reset,
  output [31:0] in_out
);

  wire clk_out;

  Clock clk (.out(clk_out));
  Register #(.width(32)) pc (.D(in_in), .en(Enable), .clk(clk_out), .Q(in_out), .clr(Reset));
endmodule

module instruction_memory (
  input  [31:0] read_adress,
  output [31:0] instruction
);

  ROM #(.addrWidth(24), .dataWidth(32)) rom_1 (.addr(read_adress[25:2]), .data(instruction));

  // Notes on the sheet:
  //   only multiple
  //   of 4
  //   0xc goes in
  //   the memory is accessed by interval of 4 and 4. So you dont need the first 2 wires
  //   the 3rd value appears (c = 12 = 4x3)
endmodule

module ALU (
  input  [31:0] alu_in_1,
  input  [31:0] alu_in_2,
  input  [3:0] alu_op
);

  wire [31:0] adder_1_out, and_1_out, nor_1_out, or_1_out, subtractor_1_out;

  Adder #(.width(32)) adder_1 (.a(alu_in_1), .b(alu_in_2), .out(adder_1_out));  // open: cin, cout
  Subtractor #(.width(32)) subtractor_1 (.a(alu_in_1), .b(alu_in_2), .out(subtractor_1_out));  // open: bin, bout
  assign and_1_out = alu_in_1 & alu_in_2;  // AND_Gate and_1, 32 bits wide
  assign or_1_out = alu_in_1 | alu_in_2;  // OR_Gate or_1, 32 bits wide
  assign nor_1_out = ~(alu_in_1 | alu_in_2);  // NOR_Gate nor_1, 32 bits wide
  Multiplexer #(.select(4), .width(32), .enable("false")) multiplexer_1 (.sel(alu_op));  // open: in0, in1, in2, in3, in4, in5, in6, in7, in8, in9, in10, in11, in12, in13, in14, in15, out

  // Notes on the sheet:
  //   fios separados do segundo reg
endmodule
